# Fritzing sketch Despertador_Diagrama (saved by Fritzing 0.9.9b)
breadboards: 2

parts:
  M1 = DOIT Esp32 DevKit v1 (30 pins long, 11 pins width) [part_number=ESP32S-PIN30]
  R1 = Resistor [tolerance=±5% power=0.25 resistance=10k package=THT]
  LED1 = LED - 5mm [color="Red (633nm)" current=0.030 package="5 mm [THT]"]
  ZS-042_RTC1 = ZS-042 RTC Module
  OLED1 = OLED 128x64 I2C Monochrome Display
  KY-1 = Keyes Relay [package=THT]
  J1 = Piezo Speaker
  S1 = Pushbutton [package="[THT]"]
  R2 = Resistor [tolerance=±5% power=0.25 resistance=10k package=THT]
  S2 = Pushbutton [package="[THT]"]
  R3 = Resistor [tolerance=±5% power=0.25 resistance=10k package=THT]
  Q1 = NPN-Transistor [package="TO92 [THT]"]
  R4 = Resistor [tolerance=±5% power=0.25 resistance=10k package=THT]
  R5 = Resistor [tolerance=±5% power=0.25 resistance=330 package=THT]
  Power_plug1 = Power plug
  M2 = DC Motor

nets:
  3V3: M1.3V3, OLED1.VDD, S1.Pin_3, S1.Pin_4
  GND: M1.GND, LED1.cathode, ZS-042_RTC1.GND, OLED1.GND, KY-1.ground, KY-1.C, J1.pin1, R2.Pin_1, S2.Pin_1, S2.Pin_2, R3.Pin_0, Q1.E, Power_plug1.GND
  N1: M1.D4, R1.Pin_1
  N2: M1.D21, ZS-042_RTC1.SDA, OLED1.SDA
  N3: M1.D22, ZS-042_RTC1.SCL, OLED1.SCK
  N4: M1.EN, S2.Pin_3, S2.Pin_4, R3.Pin_1
  N5: M1.D27, S1.Pin_1, S1.Pin_2, R2.Pin_0
  N6: M1.D12, J1.pin2
  N7: M1.D13, R5.Pin_0
  VCC: M1.VIN, ZS-042_RTC1.VCC, KY-1.power, R4.Pin_1, Power_plug1.VCC, M2.pin_1
  N8: R1.Pin_0, LED1.anode
  N9: KY-1.signal, Q1.C, R4.Pin_0
  N10: KY-1.NO, M2.pin_2
  N11: Q1.B, R5.Pin_1

custom parts:
  DOIT Esp32 DevKit v1 (30 pins long, 11 pins width): The DOIT Esp32 DevKit v1 is one of the development board created by DOIT to evaluate the ESP-WROOM-32 module. It is based on the ESP32 microcontroller that boasts Wifi, Bluetooth, Ethernet and Low Power support all in a single chip. (vanepp) made breadboard work, adjusted pin numbering and labels and reduced size of schematic and cleaned up pcb. This chip is 30pins long (2 x15) and 11 pins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
  Keyes Relay: The Keyes 5V relay module is suitable for SCM development, home appliance control. It uses a 5V~12V TIL control signal which can control DC / AC signal.
